# Fritzing sketch ImpossibleColorTest (saved by Fritzing 0.9.2b)
breadboards: 1

parts:
  Part1 = Arduino Nano (Rev3.0)
  R2 = Resistor [tolerance=±5% resistance=220 package=THT]
  R3 = Resistor [tolerance=±5% resistance=220 package=THT]
  LED1 = RGB LED (com. cathode, rgb) [package="5 mm [THT]"]
  R4 = Rotary Potentiometer (Small) [maximum_resistance=100kΩ package=THT]
  R5 = Rotary Potentiometer (Small) [maximum_resistance=100kΩ package=THT]
  R1 = Resistor [tolerance=±5% resistance=220 package=THT]

nets:
  N1: Part1.GND, LED1.common_cathode, R4.leg2, R5.leg2
  N2: Part1.D9, R3.Pin_0
  N3: Part1.D10, R2.Pin_0
  N4: Part1.D11/MOSI, R1.Pin_0
  N5: Part1.5V, R4.leg1, R5.leg1
  N6: Part1.A1, R5.wiper
  N7: Part1.A0, R4.wiper
  N8: R2.Pin_1, LED1.green_anode
  N9: R3.Pin_1, LED1.red_anode
  N10: LED1.blue_anode, R1.Pin_1

notes:
  R, B: 180 ohm
  G: 820 ohm
  5K Pot
  L: R/G mix
  R: refresh rate
  "Impossible Color" test
  SM Platt, August 2019
